// Logisim project CPU.circ as structural Verilog: 3 circuits, main circuit main
module main (
);

  wire and_1_out, and_2_out, and_3_out, and_4_out, and_5_out, and_6_out, and_7_out, and_8_out, and_9_out,
       and_10_out, and_11_out, and_12_out, and_13_out, and_14_out, and_15_out, and_16_out, and_17_out,
       and_18_out, and_19_out, and_20_out, and_21_out, and_22_out, and_23_out, and_24_out, and_25_out,
       and_26_out, and_27_out, and_28_out, and_29_out, and_30_out, and_31_out, and_32_out, and_33_out,
       and_34_out, and_35_out, and_37_out, and_38_out, and_39_out, and_40_out, and_42_out, and_45_out,
       and_47_out, and_48_out, and_49_out, and_51_out, clock_1_out, comparator_1_eq, comparator_1_gt,
       comparator_1_lt, controlled_buffer_1_out, controlled_buffer_2_out, controlled_buffer_3_out,
       decoder_1_out0, decoder_1_out1, decoder_1_out2, decoder_2_out0, decoder_2_out1, decoder_2_out2,
       decoder_2_out3, decoder_2_out4, decoder_3_out0, decoder_3_out1, decoder_3_out2, decoder_3_out3,
       decoder_4_out0, decoder_4_out1, decoder_4_out2, decoder_4_out3, decoder_4_out4, decoder_5_out1,
       decoder_5_out2, decoder_5_out3, decoder_5_out4, decoder_5_out5, decoder_5_out6, decoder_5_out7,
       decoder_5_out8, decoder_5_out9, decoder_5_out10, decoder_5_out11, decoder_5_out12, decoder_5_out13,
       decoder_5_out14, decoder_5_out15, demultiplexer_1_out0, demultiplexer_1_out1, demultiplexer_1_out2,
       keyboard_1_avail, multiplexer_1_out, not_1_out, not_2_out, not_3_out, not_4_out, not_5_out, not_6_out,
       not_7_out, not_8_out, not_9_out, not_10_out, not_11_out, not_12_out, not_13_out, not_14_out, or_1_out,
       or_2_out, or_3_out, or_4_out, or_5_out, or_6_out, or_7_out, or_8_out, or_9_out, or_10_out, or_11_out,
       or_12_out, or_13_out, or_14_out, or_15_out, register_13_q, Reset_out, Start_out, t_ff_1_q;
  wire [3:0] controlled_buffer_7_out, counter_1_q, register_4_q, register_5_q, register_6_q, register_10_q_2,
       register_10_q_3, register_12_q;
  wire [6:0] controlled_buffer_13_out, keyboard_1_data;
  wire [23:0] register_1_out, register_2_out, register_3_out;
  wire [31:0] alu_8bit_1_r, controlled_buffer_4_out, ram_1_data, ram_2_data, ram_3_data, ram_4_data,
       ram_5_data, register_7_q, register_8_q, register_9_q, register_11_q;
  wire [31:4] controlled_buffer_7_out_2;
  wire [31:7] controlled_buffer_13_out_2;
  wire [31:8] register_10_q;

  Clock clock_1 (.out(clock_1_out));
  not not_1 (not_1_out, or_13_out);
  and and_1 (and_1_out, clock_1_out, t_ff_1_q, not_1_out);
  not not_2 (not_2_out, decoder_5_out13);
  and and_2 (and_2_out, decoder_1_out0, not_2_out, and_1_out);
  and and_3 (and_3_out, decoder_1_out1, not_2_out, and_1_out);
  and and_4 (and_4_out, decoder_1_out2, not_2_out, and_1_out);
  or or_1 (or_1_out, and_45_out, and_32_out);
  and and_5 (and_5_out, and_1_out, or_1_out);
  Demultiplexer #(.select(4)) demultiplexer_1 (
    .out0(demultiplexer_1_out0), .out1(demultiplexer_1_out1), .out2(demultiplexer_1_out2), .in(and_5_out),
    .sel(register_10_q_3));  // open: out3, out4, out5, out6, out7, out8, out9, out10, out11, out12, out13, out14, out15, en
  RAM #(.addrWidth(24), .dataWidth(32), .bus("separate")) ram_1 (
    .addr(register_8_q[23:0]), .din(register_9_q), .data(ram_1_data), .clk(and_51_out), .clr(or_2_out));  // open: str, sel, ld
  Register register_1 (
    .In(ram_1_data), .S_2(demultiplexer_1_out0), .C(and_2_out), .R(or_2_out), .Out(register_1_out),
    .D(register_8_q), .S(and_45_out), .SE(demultiplexer_1_out0));
  Register register_2 (
    .In(ram_1_data), .S_2(demultiplexer_1_out1), .C(and_3_out), .R(or_2_out), .Out(register_2_out),
    .D(register_8_q), .S(and_45_out), .SE(demultiplexer_1_out1));
  Register register_3 (
    .In(ram_1_data), .S_2(demultiplexer_1_out2), .C(and_4_out), .R(or_2_out), .Out(register_3_out),
    .D(register_8_q), .S(and_45_out), .SE(demultiplexer_1_out2));
  Register_part #(.width(4)) register_4 (
    .D(controlled_buffer_7_out), .Q(register_4_q), .clk(and_6_out), .clr(or_2_out));  // open: en
  and and_6 (and_6_out, and_1_out, and_49_out);
  TTY #(.rows(15)) tty_1 (.data(controlled_buffer_13_out), .clk(and_42_out), .clr(or_2_out));  // open: we
  RAM #(.addrWidth(24), .dataWidth(32), .bus("separate")) ram_2 (
    .addr(register_1_out), .din(register_9_q), .data(ram_2_data), .clk(controlled_buffer_1_out));  // open: str, sel, ld, clr
  assign controlled_buffer_1_out = demultiplexer_1_out0 ? and_7_out : 1'bz;  // Controlled_Buffer controlled_buffer_1
  RAM #(.addrWidth(24), .dataWidth(32), .bus("separate")) ram_3 (
    .addr(register_2_out), .din(register_9_q), .data(ram_3_data), .clk(controlled_buffer_2_out));  // open: str, sel, ld, clr
  assign controlled_buffer_2_out = demultiplexer_1_out1 ? and_7_out : 1'bz;  // Controlled_Buffer controlled_buffer_2
  RAM #(.addrWidth(24), .dataWidth(32), .bus("separate")) ram_4 (
    .addr(register_3_out), .din(register_9_q), .data(ram_4_data), .clk(controlled_buffer_3_out));  // open: str, sel, ld, clr
  assign controlled_buffer_3_out = demultiplexer_1_out2 ? and_7_out : 1'bz;  // Controlled_Buffer controlled_buffer_3
  Keyboard keyboard_1 (.clk(not_3_out), .clr(or_2_out), .avail(keyboard_1_avail), .data(keyboard_1_data));  // open: re
  Decoder #(.select(4)) decoder_1 (
    .out0(decoder_1_out0), .out1(decoder_1_out1), .out2(decoder_1_out2), .sel(register_4_q));  // open: out3, out4, out5, out6, out7, out8, out9, out10, out11, out12, out13, out14, out15, en
  assign controlled_buffer_4_out = decoder_1_out0 ? ram_2_data : 32'bz;  // Controlled_Buffer controlled_buffer_4
  assign controlled_buffer_4_out = decoder_1_out1 ? ram_3_data : 32'bz;  // Controlled_Buffer controlled_buffer_5
  assign controlled_buffer_4_out = decoder_1_out2 ? ram_4_data : 32'bz;  // Controlled_Buffer controlled_buffer_6
  not not_3 (not_3_out, and_38_out);
  and and_7 (and_7_out, not_4_out, and_45_out);
  not not_4 (not_4_out, and_1_out);
  Button Start (.out(Start_out));
  Button Reset (.out(Reset_out));
  not not_5 (not_5_out, t_ff_1_q);
  T_Flip_Flop t_ff_1 (.clk(Start_out), .T(1'b1), .Q(t_ff_1_q));  // open: Qn, preset, reset, en
  Hex_Digit_Display hex_digit_display_1 (.value(register_10_q_3));  // open: dp
  Hex_Digit_Display hex_digit_display_2 (.value(register_10_q_2));  // open: dp
  or or_2 (or_2_out, not_5_out, Reset_out);
  Decoder #(.select(4)) decoder_2 (
    .out0(decoder_2_out0), .out1(decoder_2_out1), .out2(decoder_2_out2), .out3(decoder_2_out3),
    .out4(decoder_2_out4), .sel(register_5_q));  // open: out5, out6, out7, out8, out9, out10, out11, out12, out13, out14, out15, en
  Register_part #(.width(4)) register_5 (
    .D(controlled_buffer_4_out[3:0]), .Q(register_5_q), .clk(not_8_out), .clr(or_2_out));  // open: en
  Counter #(.width(4), .max('hf)) counter_1 (
    .Q(counter_1_q), .clk(and_1_out), .clr(or_3_out));  // open: load, D, count, carry
  or or_3 (or_3_out, or_2_out, and_6_out, and_29_out, decoder_3_out3);
  assign {controlled_buffer_7_out_2, controlled_buffer_7_out} = or_12_out ? controlled_buffer_4_out : 32'bz;  // Controlled_Buffer controlled_buffer_7
  Decoder #(.select(4)) decoder_3 (
    .out0(decoder_3_out0), .out1(decoder_3_out1), .out2(decoder_3_out2), .out3(decoder_3_out3),
    .sel(counter_1_q));  // open: out4, out5, out6, out7, out8, out9, out10, out11, out12, out13, out14, out15, en
  Register_part #(.width(4)) register_6 (
    .D(controlled_buffer_4_out[3:0]), .Q(register_6_q), .clk(not_7_out), .clr(or_2_out));  // open: en
  Decoder #(.select(4)) decoder_4 (
    .out0(decoder_4_out0), .out1(decoder_4_out1), .out2(decoder_4_out2), .out3(decoder_4_out3),
    .out4(decoder_4_out4), .sel(register_6_q));  // open: out5, out6, out7, out8, out9, out10, out11, out12, out13, out14, out15, en
  Register_part #(.width(32)) register_7 (
    .D({controlled_buffer_7_out_2, controlled_buffer_7_out}), .Q(register_7_q), .clk(and_8_out),
    .clr(or_2_out));  // open: en
  and and_8 (and_8_out, decoder_2_out0, or_10_out);
  and and_9 (and_9_out, or_6_out, decoder_4_out0);
  Register_part #(.width(32)) register_8 (
    .D({controlled_buffer_7_out_2, controlled_buffer_7_out}), .Q(register_8_q), .clk(and_10_out),
    .clr(or_2_out));  // open: en
  or or_4 (or_4_out, and_45_out, and_11_out);
  and and_10 (and_10_out, decoder_2_out1, or_10_out);
  and and_11 (and_11_out, or_6_out, decoder_4_out1);
  Register_part #(.width(32)) register_9 (
    .D({controlled_buffer_7_out_2, controlled_buffer_7_out}), .Q(register_9_q), .clk(and_12_out),
    .clr(or_2_out));  // open: en
  and and_12 (and_12_out, decoder_2_out2, or_10_out);
  and and_13 (and_13_out, or_6_out, decoder_4_out2);
  Register_part #(.width(32)) register_10 (
    .D({controlled_buffer_7_out_2, controlled_buffer_7_out}),
    .Q({register_10_q, register_10_q_2, register_10_q_3}), .clk(or_5_out), .clr(or_2_out));  // open: en
  or or_5 (or_5_out, and_15_out, and_33_out);
  and and_14 (and_14_out, or_6_out, decoder_4_out3);
  and and_15 (and_15_out, decoder_2_out3, or_10_out);
  Register_part #(.width(32)) register_11 (
    .D({controlled_buffer_7_out_2, controlled_buffer_7_out}), .Q(register_11_q), .clk(and_16_out),
    .clr(or_2_out));  // open: en
  and and_16 (and_16_out, decoder_2_out4, or_10_out);
  and and_17 (and_17_out, or_6_out, decoder_4_out4);
  Register_part #(.width(4)) register_12 (
    .D(controlled_buffer_4_out[3:0]), .Q(register_12_q), .clk(not_6_out), .clr(or_2_out));  // open: en
  not not_6 (not_6_out, decoder_3_out0);
  assign {controlled_buffer_7_out_2, controlled_buffer_7_out} = and_9_out ? register_7_q : 32'bz;  // Controlled_Buffer controlled_buffer_8
  assign {controlled_buffer_7_out_2, controlled_buffer_7_out} = or_4_out ? register_8_q : 32'bz;  // Controlled_Buffer controlled_buffer_9
  assign {controlled_buffer_7_out_2, controlled_buffer_7_out} = and_13_out ? register_9_q : 32'bz;  // Controlled_Buffer controlled_buffer_10
  assign {controlled_buffer_7_out_2, controlled_buffer_7_out} = and_14_out ? {register_10_q, register_10_q_2, register_10_q_3} : 32'bz;  // Controlled_Buffer controlled_buffer_11
  assign {controlled_buffer_7_out_2, controlled_buffer_7_out} = and_17_out ? register_11_q : 32'bz;  // Controlled_Buffer controlled_buffer_12
  not not_7 (not_7_out, and_18_out);
  or or_6 (or_6_out, and_37_out, and_20_out);
  or or_7 (or_7_out, and_26_out, and_48_out, and_39_out, and_40_out, and_32_out);
  and and_18 (and_18_out, or_7_out, and_1_out);
  not not_8 (not_8_out, and_19_out);
  and and_19 (and_19_out, and_1_out, or_8_out);
  or or_8 (or_8_out, and_24_out, and_28_out, and_34_out, and_37_out);
  or or_9 (or_9_out, and_25_out, and_49_out, and_38_out, and_48_out, and_29_out);
  and and_20 (and_20_out, or_9_out, and_1_out);
  and and_21 (and_21_out, and_1_out, or_11_out);
  or or_10 (or_10_out, and_37_out, and_21_out);
  or or_11 (or_11_out, and_22_out, and_27_out, and_35_out);
  Comparator #(.width(32)) comparator_1 (
    .a(register_8_q), .b(register_9_q), .gt(comparator_1_gt), .eq(comparator_1_eq), .lt(comparator_1_lt));
  buf or_12 (or_12_out, and_22_out);  // OR_Gate
  not not_9 (not_9_out, comparator_1_gt);
  not not_10 (not_10_out, comparator_1_eq);
  not not_11 (not_11_out, comparator_1_lt);
  Decoder #(.select(4)) decoder_5 (
    .out1(decoder_5_out1), .out2(decoder_5_out2), .out3(decoder_5_out3), .out4(decoder_5_out4),
    .out5(decoder_5_out5), .out6(decoder_5_out6), .out7(decoder_5_out7), .out8(decoder_5_out8),
    .out9(decoder_5_out9), .out10(decoder_5_out10), .out11(decoder_5_out11), .out12(decoder_5_out12),
    .out13(decoder_5_out13), .out14(decoder_5_out14), .out15(decoder_5_out15), .sel(register_12_q));  // open: out0, en
  and and_22 (and_22_out, decoder_3_out2, decoder_5_out14);
  not not_12 (not_12_out, and_30_out);
  assign {controlled_buffer_13_out_2, controlled_buffer_13_out} = and_38_out ? {controlled_buffer_7_out_2, controlled_buffer_7_out} : 32'bz;  // Controlled_Buffer controlled_buffer_13
  assign {controlled_buffer_7_out_2, controlled_buffer_7_out} = and_33_out ? alu_8bit_1_r : 32'bz;  // Controlled_Buffer controlled_buffer_14
  Register_part #(.width(1)) register_13 (
    .D(multiplexer_1_out), .Q(register_13_q), .clk(and_23_out), .clr(or_2_out));  // open: en
  Multiplexer #(.select(3)) multiplexer_1 (
    .in0(comparator_1_gt), .in1(comparator_1_eq), .in2(comparator_1_lt), .in3(not_9_out), .in4(not_10_out),
    .in5(not_11_out), .in6(1'b1), .in7(1'b0), .out(multiplexer_1_out), .sel(register_10_q_3[2:0]));  // open: en
  and and_23 (and_23_out, not_14_out, decoder_5_out11);
  and and_24 (and_24_out, decoder_3_out1, decoder_5_out14);
  and and_25 (and_25_out, decoder_3_out2, decoder_5_out1);
  and and_26 (and_26_out, decoder_3_out1, decoder_5_out1);
  RAM #(.addrWidth(24), .dataWidth(32), .bus("separate")) ram_5 (
    .addr(register_11_q[23:0]), .din({controlled_buffer_7_out_2, controlled_buffer_7_out}),
    .data(ram_5_data), .clk(not_12_out), .clr(or_2_out));  // open: str, sel, ld
  ALU_8bit alu_8bit_1 (.A(register_8_q), .R(alu_8bit_1_r), .B(register_9_q), .OP(register_7_q), .Clock(and_1_out));
  assign {controlled_buffer_7_out_2, controlled_buffer_7_out} = and_35_out ? {{25{1'b0}}, keyboard_1_data} : 32'bz;  // Controlled_Buffer controlled_buffer_15
  or or_13 (or_13_out, decoder_5_out15, and_31_out);
  and and_27 (and_27_out, decoder_3_out2, decoder_5_out2);
  and and_28 (and_28_out, decoder_3_out1, decoder_5_out2);
  and and_29 (and_29_out, decoder_3_out2, register_13_q, decoder_5_out3);
  buf or_14 (or_14_out, and_25_out);  // OR_Gate
  and and_30 (and_30_out, and_1_out, or_14_out);
  and and_31 (and_31_out, and_47_out, not_13_out);
  not not_13 (not_13_out, keyboard_1_avail);
  and and_32 (and_32_out, decoder_3_out1, register_13_q, decoder_5_out3);
  and and_33 (and_33_out, decoder_3_out2, decoder_5_out4);
  buf or_15 (or_15_out, and_27_out);  // OR_Gate
  assign {controlled_buffer_7_out_2, controlled_buffer_7_out} = or_15_out ? ram_5_data : 32'bz;  // Controlled_Buffer controlled_buffer_16
  and and_34 (and_34_out, decoder_3_out1, decoder_5_out5);
  and and_35 (and_35_out, decoder_3_out2, decoder_5_out5);
  // AND_Gate and_36 has open pins: in0=decoder_3_out1, in1=decoder_5_out4, out=open
  and and_37 (and_37_out, decoder_3_out2, decoder_5_out7);
  and and_38 (and_38_out, decoder_3_out2, decoder_5_out6);
  and and_39 (and_39_out, decoder_3_out1, decoder_5_out6);
  not not_14 (not_14_out, and_1_out);
  and and_40 (and_40_out, decoder_3_out1, decoder_5_out7);
  // AND_Gate and_41 has open pins: in0=decoder_3_out2, in1=decoder_5_out8, out=open
  and and_42 (and_42_out, and_38_out, not_14_out);
  // AND_Gate and_43 has open pins: in0=decoder_3_out2, in1=decoder_5_out9, out=open
  // AND_Gate and_44 has open pins: in0=decoder_3_out1, in1=decoder_5_out9, out=open
  and and_45 (and_45_out, decoder_3_out1, decoder_5_out8);
  // AND_Gate and_46 has open pins: in0=decoder_3_out1, in1=decoder_5_out10, out=open
  and and_47 (and_47_out, decoder_3_out2, decoder_5_out10);
  and and_48 (and_48_out, decoder_5_out13, decoder_3_out1);
  and and_49 (and_49_out, decoder_5_out13, decoder_3_out2);
  // AND_Gate and_50 has open pins: in0=decoder_3_out1, in1=decoder_5_out12, out=open
  and and_51 (and_51_out, decoder_3_out2, decoder_5_out12);

  // Notes on the sheet:
  //   MMU
  //   BIOS
  //   HDD1
  //   HDD2
  //   Terminal
  //   Keyboard
  //   GET
  //   R0
  //   R1
  //   R2
  //   R3
  //   R4
  //   PUT
  //   Compare
  //   ALU
  //   RAM
  //   Decoder
endmodule

module ALU_8bit (
  input  [31:0] OP,
  input  [31:0] A,
  input  [31:0] B,
  input  Clock,
  output [31:0] R
);

  wire [31:0] adder_1_out, and_1_out, divider_1_out, multiplier_1_out, nand_1_out, nor_1_out, not_1_out,
       or_1_out, random_1_out, subtractor_1_out, xor_1_out;

  assign and_1_out = A & B;  // AND_Gate and_1, 32 bits wide
  assign or_1_out = A | B;  // OR_Gate or_1, 32 bits wide
  assign xor_1_out = A ^ B;  // XOR_Gate xor_1, 32 bits wide
  assign nand_1_out = ~(A & B);  // NAND_Gate nand_1, 32 bits wide
  assign nor_1_out = ~(A | B);  // NOR_Gate nor_1, 32 bits wide
  Adder #(.width(32)) adder_1 (.a(A), .b(B), .out(adder_1_out));  // open: cin, cout
  Subtractor #(.width(32)) subtractor_1 (.a(A), .b(B), .out(subtractor_1_out));  // open: bin, bout
  Multiplier #(.width(32)) multiplier_1 (.a(A), .b(B), .out(multiplier_1_out));  // open: cin, cout
  Divider #(.width(32)) divider_1 (.a(A), .b(B), .out(divider_1_out));  // open: upper, rem
  Random #(.width(32), .seed(213)) random_1 (.clk(Clock), .out(random_1_out));  // open: next, clr
  assign not_1_out = ~A;  // NOT_Gate not_1, 32 bits wide
  Multiplexer #(.select(4), .width(32)) multiplexer_1 (
    .in0(A), .in1(not_1_out), .in2(and_1_out), .in3(or_1_out), .in4(xor_1_out), .in5(nand_1_out),
    .in6(nor_1_out), .in7({32{1'b1}}), .in8({32{1'b0}}), .in9(adder_1_out), .in10(subtractor_1_out),
    .in11(multiplier_1_out), .in12(divider_1_out), .in13(random_1_out), .out(R), .sel(OP[3:0]));  // open: in14, in15, en
endmodule

module Register (
  input  [31:0] D,
  input  SE,
  input  S,
  input  [31:0] In,
  input  S_2,
  input  C,
  input  R,
  output [23:0] Out
);

  wire and_1_out, controlled_buffer_1_out, not_1_out, not_2_out, not_3_out, or_1_out, t_ff_1_q;
  wire [23:0] counter_1_q;

  not not_1 (not_1_out, S);
  not not_2 (not_2_out, not_1_out);
  assign controlled_buffer_1_out = not_2_out ? 1'b0 : 1'bz;  // Controlled_Buffer controlled_buffer_1
  assign controlled_buffer_1_out = not_1_out ? S_2 : 1'bz;  // Controlled_Buffer controlled_buffer_2
  Counter #(.width(24), .max('hffffff)) counter_1 (
    .load(controlled_buffer_1_out), .D(In[23:0]), .count(t_ff_1_q), .Q(counter_1_q), .clk(or_1_out), .clr(R));  // open: carry
  or or_1 (or_1_out, controlled_buffer_1_out, t_ff_1_q);
  T_Flip_Flop t_ff_1 (.clk(C), .T(1'b1), .Q(t_ff_1_q), .reset(t_ff_1_q));  // open: Qn, preset, en
  and and_1 (and_1_out, S, SE);
  assign Out = and_1_out ? D[23:0] : 24'bz;  // Controlled_Buffer controlled_buffer_3
  assign Out = not_3_out ? counter_1_q : 24'bz;  // Controlled_Buffer controlled_buffer_4
  not not_3 (not_3_out, and_1_out);
endmodule
